# Fritzing sketch Connexion_Arduino_BT (saved by Fritzing 0.9.3b)
breadboards: 1

parts:
  Composant1 = Arduino Leonardo (Rev3b)
  Composant2 = Bluetooth HC-06
  R1 = Resistor [tolerance=±5% resistance=1k package=THT]
  R2 = Resistor [tolerance=±5% resistance=2k package=THT]

nets:
  N1: Composant1.D0/RX, Composant2.TXD
  N2: Composant1.D1/TX, R1.Pin_1
  5V: Composant1.5V, Composant2.VCC
  GND: Composant1.GND, Composant2.GND, R2.Pin_0
  N3: Composant2.RXD, R1.Pin_0, R2.Pin_1

notes:
  1K ohm
  2K ohm
