# Fritzing sketch Connexion_Arduino_WiFi (saved by Fritzing 0.9.3b)
breadboards: 1

parts:
  Composant1 = Arduino Leonardo (Rev3b)
  R1 = Resistor [tolerance=±5% resistance=10k package=THT]
  R2 = Resistor [tolerance=±5% resistance=20k package=THT]
  Espessif_Serial_Wifi_Modul_1 = ESP8266 ESP01 [part_number=ESP8266 package=THT]

nets:
  N1: Composant1.D1/TX, R1.Pin_1
  3V3: Composant1.3V3, Espessif_Serial_Wifi_Modul_1.VCC, Espessif_Serial_Wifi_Modul_1.CH_PD
  GND: Composant1.GND, R2.Pin_0, Espessif_Serial_Wifi_Modul_1.GND
  N2: Composant1.D11_PWM, Espessif_Serial_Wifi_Modul_1.TXD
  N3: R1.Pin_0, R2.Pin_1, Espessif_Serial_Wifi_Modul_1.RXD

notes:
  10K ohm
  20K ohm

custom parts:
  ESP8266 ESP01: Generic WiFi Module based on the ESP8266 with onboard PCB antenna and UART communications
