# Fritzing sketch cablageWatering (saved by Fritzing 0.9.3b)
breadboards: 1

parts:
  Composant1 = Arduino Uno (Rev3)  # not connected
  Composant2 = Soil Moisture Sensor
  Composant3 = Soil Moisture Sensor
  Composant4 = Soil Moisture Sensor
  Composant5 = Soil Moisture Sensor
  R1 = Resistor [tolerance=±5% resistance=10 package=THT]
  Espessif_Serial_Wifi_Modul_1 = ESP8266 ESP01 [part_number=ESP8266 package=THT]
  M1 = DC Motor [part_number=Waterpump]
  M2 = DC Motor [part_number=Waterpump]
  M3 = DC Motor [part_number=Waterpump]
  M4 = DC Motor [part_number=Waterpump]
  RelayShield1 = SeeedStudio - Relay Shield v3.0
  R2 = Resistor [tolerance=±5% resistance=10 package=THT]
  R3 = Resistor [tolerance=±5% resistance=10 package=THT]
  R4 = Resistor [tolerance=±5% resistance=10 package=THT]
  R5 = Resistor [tolerance=±5% resistance=100 package=THT]

nets:
  VCC: Composant2.VCC, Composant3.VCC, Composant4.VCC, Composant5.VCC, RelayShield1.5V
  N1: Composant2.SIG, RelayShield1.A0
  GND: Composant2.GND, Composant3.GND, Composant4.GND, Composant5.GND, R1.Pin_1, Espessif_Serial_Wifi_Modul_1.GND, RelayShield1.GND
  N2: Composant3.SIG, RelayShield1.A1
  N3: Composant4.SIG, RelayShield1.A2
  N4: Composant5.SIG, RelayShield1.A3
  N5: R1.Pin_0, R2.Pin_1
  N6: Espessif_Serial_Wifi_Modul_1.RXD, R2.Pin_0, R4.Pin_1
  N7: Espessif_Serial_Wifi_Modul_1.TXD, RelayShield1.D8
  VCC_2: Espessif_Serial_Wifi_Modul_1.VCC, Espessif_Serial_Wifi_Modul_1.CH_PD, RelayShield1.3V3, R5.Pin_0, R5.Pin_1
  N8: M1.pin_2, RelayShield1.NO4
  N9: M2.pin_2, RelayShield1.NO2
  N10: M3.pin_2, RelayShield1.NO3
  N11: M4.pin_2, RelayShield1.NO1
  N12: RelayShield1.D9_PWM, R4.Pin_0
  N13: RelayShield1.NC4, R3.Pin_1

notes:
  shield positionné sur arduino UNO
  prise de courant
  + -
  SIG VCC GND
  capteur water level
  GP1A73A1 ou GP1A73A

custom parts:
  ESP8266 ESP01: Generic WiFi Module based on the ESP8266 with onboard PCB antenna and UART communications
  SeeedStudio - Relay Shield v3.0: Description TheRelay Shield provides four high quality relay that can control high current loads to Arduino / Seeeduino boards. It also provides NO (Normally Open) / NC (Normally Closed) interface. It could be a nice solution for controlling devices that could not be directly controlled by Arduino's Digital I/Os. Standardized shield form factor enables smooth connection with Arduino and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
