# Fritzing sketch SmartWatering (saved by Fritzing 0.9.3b)
breadboards: 3

parts:
  Composant1 = Arduino Leonardo (Rev3b)  # not connected
  RelayShield1 = SeeedStudio - Relay Shield v3.0
  M1 = DC Motor
  M2 = DC Motor
  M3 = DC Motor
  Composant2 = Soil Moisture Sensor
  Composant3 = Soil Moisture Sensor
  Composant4 = Soil Moisture Sensor
  Composant5 = Soil Moisture Sensor

nets:
  N1: RelayShield1.A0, Composant2.SIG
  N2: RelayShield1.A1, Composant3.SIG
  N3: RelayShield1.A2, Composant4.SIG
  N4: RelayShield1.A3, Composant5.SIG
  GND: RelayShield1.GND, Composant2.GND, Composant3.GND, Composant4.GND, Composant5.GND
  N5: RelayShield1.COM1, RelayShield1.COM2, RelayShield1.COM3
  N6: RelayShield1.NO1, M1.pin_2
  N7: RelayShield1.NO2, M2.pin_2
  N8: RelayShield1.NO3, M3.pin_2
  N9: M1.pin_1, M2.pin_1, M3.pin_1
  VCC: Composant2.VCC, Composant3.VCC, Composant4.VCC, Composant5.VCC

notes:
  Prise Electrique

custom parts:
  SeeedStudio - Relay Shield v3.0: Description TheRelay Shield provides four high quality relay that can control high current loads to Arduino / Seeeduino boards. It also provides NO (Normally Open) / NC (Normally Closed) interface. It could be a nice solution for controlling devices that could not be directly controlled by Arduino's Digital I/Os. Standardized shield form factor enables smooth connection with Arduino and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
